# Fritzing sketch ECG_test (saved by Fritzing 0.9.6b)
breadboards: 1

parts:
  Part1 = Arduino Uno (Rev3)
  U1 = POT [package=pot_alpha_rv16af-20]
  R1 = Resistor [tolerance=±5% power=0.25 resistance=220 package=THT]
  LED2 = LED - 5mm [color="Red (633nm)" current=0.030 package="5 mm [THT]"]

nets:
  N1: Part1.A0, U1.S
  N2: Part1.D9_PWM, LED2.cathode
  N3: Part1.5V, U1.E
  N4: Part1.GND, U1.A, R1.Pin_0
  N5: R1.Pin_1, LED2.anode
